// Logisim project checkpoint.circ as structural Verilog: 4 circuits, main circuit main
module main (
  input  [3:0] bus_0,
  input  [3:0] bus_0_2
);

  wire cdm_16_1_p1, cdm_16_1_p2, cdm_16_1_p4, cdm_16_1_p5, cdm_16_1_p6, cdm_16_1_p7, cdm_16_1_p8,
       cdm_16_1_p9, clock, mem, not_1_out, ram_1_p4, rd, word;
  wire [3:0] joystick_1_x, joystick_1_y;
  wire [15:0] _1t1_x, _1t1_y, _1t2_x, _1t2_y, _2t1_x, _2t1_y, _2t2_x, _2t2_y, _2t3_x, _2t3_y, _3, _4, _5, _6,
       addr, cdm_16_1_p15, controlled_buffer_2_out, data, mario_x, mario_y, out;

  // Debugger debugger_1: pin names not known
  Joystick joystick_1 (.x(joystick_1_x), .y(joystick_1_y));
  // Probe on joystick_1_x
  // Probe on cdm_16_1_p5
  // Probe on cdm_16_1_p4
  // Probe on cdm_16_1_p2
  // Probe on cdm_16_1_p1
  // CdM_16 cdm_16_1: pin names not known; wires that end beside it: cdm_16_1_p1, cdm_16_1_p2, clock, cdm_16_1_p4, cdm_16_1_p5, cdm_16_1_p6, cdm_16_1_p7, cdm_16_1_p8, cdm_16_1_p9, mem, rd, word, addr, out, cdm_16_1_p15
  // Probe on joystick_1_y
  // Probe on cdm_16_1_p6
  // Probe on cdm_16_1_p7
  Clock clock_1 (.out(clock));
  // Probe on cdm_16_1_p8
  // Probe on cdm_16_1_p9
  joystick joystick_2 (
    .bus_0(cdm_16_1_p15), .input_1(bus_0), .input_2(bus_0_2), .addr(addr), .data(controlled_buffer_2_out),
    .mem(mem), .rd(rd));
  not not_1 (not_1_out, rd);
  assign data = not_1_out ? out : 16'bz;  // Controlled_Buffer controlled_buffer_1
  assign controlled_buffer_2_out = rd ? data : 16'bz;  // Controlled_Buffer controlled_buffer_2
  // Probe on _5
  // Probe on _6
  // Probe on _4
  // Probe on _3
  // Probe on _2t3_y
  // Probe on _2t3_x
  // RAM ram_1: pin names not known; wires that end beside it: addr, word, mem, ram_1_p4, rd, data
  Clock clock_2 (.out(ram_1_p4));
  // Probe on addr
  // Probe on _2t3_x
  // Probe on _2t3_y
  // Probe on mario_x
  distribute_regs distribute_regs_1 (
    .addr(addr), .out(out), .bus_0(mario_x), .clock(clock), .bus_0_2(mario_y), .bus_0_3(_1t1_x),
    .bus_0_4(_1t1_y), .bus_0_5(_1t2_x), .bus_0_6(_1t2_y), .bus_0_7(_2t1_x), .mem(mem), .bus_0_8(_2t1_y),
    .bus_0_9(_2t2_x), .bus_0_10(_2t2_y), .bus_0_11(_2t3_x), .bus_0_12(_2t3_y), .bus_0_13(_3), .bus_0_14(_4),
    .bus_0_15(_5), .bus_0_16(_6), .rd(rd));
  // Probe on mario_x
  // Probe on mario_y
  // Probe on _1t1_x
  // Probe on _1t1_y
  // Probe on _1t2_x
  // Probe on _1t2_y
  // Probe on _2t1_x
  // Probe on _2t1_y
  // Probe on _2t2_x
  // Probe on _2t2_y
endmodule

module register (
  input  [15:0] bus_0,
  input  clo,
  input  [15:0] \input ,
  output [15:0] bus_0_2
);

  wire comparator_1_lt;
  wire [15:0] multiplexer_1_out;

  Comparator #(.width(16), .mode("unsigned")) comparator_1 (
    .a({16{1'b0}}), .b(\input ), .lt(comparator_1_lt));  // open: gt, eq
  Multiplexer #(.width(16), .enable("false")) multiplexer_1 (
    .in0(bus_0_2), .in1(bus_0), .out(multiplexer_1_out), .sel(comparator_1_lt));
  Register #(.width(16)) register_1 (.D(multiplexer_1_out), .Q(bus_0_2), .clk(clo));  // open: en, clr
endmodule

module distribute_regs (
  input  [15:0] addr,
  input  [15:0] out,
  input  clock,
  input  mem,
  input  rd,
  output [15:0] bus_0,
  output [15:0] bus_0_2,
  output [15:0] bus_0_3,
  output [15:0] bus_0_4,
  output [15:0] bus_0_5,
  output [15:0] bus_0_6,
  output [15:0] bus_0_7,
  output [15:0] bus_0_8,
  output [15:0] bus_0_9,
  output [15:0] bus_0_10,
  output [15:0] bus_0_11,
  output [15:0] bus_0_12,
  output [15:0] bus_0_13,
  output [15:0] bus_0_14,
  output [15:0] bus_0_15,
  output [15:0] bus_0_16
);

  wire and_1_out, comparator_1_eq, comparator_1_gt, comparator_2_lt, or_1_out;
  wire [3:0] multiplexer_1_out;
  wire [15:0] demultiplexer_1_out0, demultiplexer_1_out1, demultiplexer_1_out2, demultiplexer_1_out3,
       demultiplexer_1_out4, demultiplexer_1_out5, demultiplexer_1_out6, demultiplexer_1_out7,
       demultiplexer_1_out8, demultiplexer_1_out9, demultiplexer_1_out10, demultiplexer_1_out11,
       demultiplexer_1_out12, demultiplexer_1_out13, demultiplexer_1_out14, demultiplexer_1_out15,
       subtractor_1_out;

  Subtractor #(.width(16)) subtractor_1 (.a(addr), .b(16'hff00), .out(subtractor_1_out));  // open: bin, bout
  // Probe on addr
  // Probe on addr
  // Probe on multiplexer_1_out
  Multiplexer #(.width(4), .enable("false")) multiplexer_1 (
    .in1(subtractor_1_out[3:0]), .out(multiplexer_1_out), .sel(and_1_out));  // open: in0
  Comparator #(.width(16), .mode("unsigned")) comparator_1 (
    .a(addr), .b(16'hff00), .gt(comparator_1_gt), .eq(comparator_1_eq));  // open: lt
  Comparator #(.width(16), .mode("unsigned")) comparator_2 (
    .a(addr), .b(16'hff10), .lt(comparator_2_lt));  // open: gt, eq
  Demultiplexer #(.select(4), .width(16), .enable("false")) demultiplexer_1 (
    .out0(demultiplexer_1_out0), .out1(demultiplexer_1_out1), .out2(demultiplexer_1_out2),
    .out3(demultiplexer_1_out3), .out4(demultiplexer_1_out4), .out5(demultiplexer_1_out5),
    .out6(demultiplexer_1_out6), .out7(demultiplexer_1_out7), .out8(demultiplexer_1_out8),
    .out9(demultiplexer_1_out9), .out10(demultiplexer_1_out10), .out11(demultiplexer_1_out11),
    .out12(demultiplexer_1_out12), .out13(demultiplexer_1_out13), .out14(demultiplexer_1_out14),
    .out15(demultiplexer_1_out15), .in(out), .sel(multiplexer_1_out));
  // Probe on and_1_out
  and and_1 (and_1_out, or_1_out, ~rd, mem, comparator_2_lt);  // AND_Gate
  or or_1 (or_1_out, comparator_1_gt, comparator_1_eq);
  register register_1 (.bus_0(demultiplexer_1_out0), .\input (demultiplexer_1_out0), .bus_0_2(bus_0), .clo(clock));
  register register_2 (.bus_0(demultiplexer_1_out1), .\input (demultiplexer_1_out1), .bus_0_2(bus_0_2), .clo(clock));
  register register_3 (.bus_0(demultiplexer_1_out15), .\input (demultiplexer_1_out15), .bus_0_2(bus_0_16), .clo(clock));
  register register_4 (.bus_0(demultiplexer_1_out2), .\input (demultiplexer_1_out2), .bus_0_2(bus_0_3), .clo(clock));
  register register_5 (.bus_0(demultiplexer_1_out3), .\input (demultiplexer_1_out3), .bus_0_2(bus_0_4), .clo(clock));
  register register_6 (.bus_0(demultiplexer_1_out4), .\input (demultiplexer_1_out4), .bus_0_2(bus_0_5), .clo(clock));
  register register_7 (.bus_0(demultiplexer_1_out5), .\input (demultiplexer_1_out5), .bus_0_2(bus_0_6), .clo(clock));
  register register_8 (.bus_0(demultiplexer_1_out6), .\input (demultiplexer_1_out6), .bus_0_2(bus_0_7), .clo(clock));
  register register_9 (.bus_0(demultiplexer_1_out7), .\input (demultiplexer_1_out7), .bus_0_2(bus_0_8), .clo(clock));
  register register_10 (.bus_0(demultiplexer_1_out8), .\input (demultiplexer_1_out8), .bus_0_2(bus_0_9), .clo(clock));
  register register_11 (.bus_0(demultiplexer_1_out9), .\input (demultiplexer_1_out9), .bus_0_2(bus_0_10), .clo(clock));
  register register_12 (
    .bus_0(demultiplexer_1_out10), .\input (demultiplexer_1_out10), .bus_0_2(bus_0_11), .clo(clock));
  register register_13 (
    .bus_0(demultiplexer_1_out11), .\input (demultiplexer_1_out11), .bus_0_2(bus_0_12), .clo(clock));
  register register_14 (
    .bus_0(demultiplexer_1_out12), .\input (demultiplexer_1_out12), .bus_0_2(bus_0_13), .clo(clock));
  register register_15 (
    .bus_0(demultiplexer_1_out13), .\input (demultiplexer_1_out13), .bus_0_2(bus_0_14), .clo(clock));
  register register_16 (
    .bus_0(demultiplexer_1_out14), .\input (demultiplexer_1_out14), .bus_0_2(bus_0_15), .clo(clock));
endmodule

module joystick (
  input  [15:0] addr,
  input  [15:0] data,
  input  mem,
  input  rd,
  input  [3:0] input_1,
  input  [3:0] input_2,
  output [15:0] bus_0
);

  wire and_1_out, comparator_1_eq, comparator_1_gt, comparator_2_lt, comparator_3_lt, comparator_4_gt,
       comparator_5_lt, comparator_6_gt, or_1_out;
  wire [15:0] multiplexer_2_out, multiplexer_3_out, multiplexer_4_out, multiplexer_5_out, multiplexer_6_out,
       subtractor_1_out;

  // Probe on addr
  // Probe on addr
  or or_1 (or_1_out, comparator_1_gt, comparator_1_eq);
  Comparator #(.width(16), .mode("unsigned")) comparator_1 (
    .a(addr), .b(16'hfefe), .gt(comparator_1_gt), .eq(comparator_1_eq));  // open: lt
  Comparator #(.width(16), .mode("unsigned")) comparator_2 (
    .a(addr), .b(16'hff00), .lt(comparator_2_lt));  // open: gt, eq
  and and_1 (and_1_out, or_1_out, comparator_2_lt, rd, mem);
  Multiplexer #(.width(16), .enable("false")) multiplexer_1 (
    .in0(data), .in1(multiplexer_3_out), .out(bus_0), .sel(and_1_out));
  Subtractor #(.width(16)) subtractor_1 (.a(addr), .b(16'hffee), .out(subtractor_1_out));  // open: bin, bout
  // Probe on input_1
  // Probe on input_1
  Multiplexer #(.width(16), .enable("false")) multiplexer_2 (
    .in0(multiplexer_4_out), .in1({16{1'b1}}), .out(multiplexer_2_out), .sel(comparator_3_lt));
  Multiplexer #(.width(16), .enable("false")) multiplexer_3 (
    .in0(multiplexer_2_out), .in1(multiplexer_5_out), .out(multiplexer_3_out), .sel(subtractor_1_out[0]));
  Comparator #(.width(4), .mode("unsigned")) comparator_3 (
    .a(input_1), .b(4'b0101), .lt(comparator_3_lt));  // open: gt, eq
  Comparator #(.width(4), .mode("unsigned")) comparator_4 (
    .a(input_1), .b(4'b1011), .gt(comparator_4_gt));  // open: eq, lt
  Comparator #(.width(4), .mode("unsigned")) comparator_5 (
    .a(input_2), .b(4'b0101), .lt(comparator_5_lt));  // open: gt, eq
  Comparator #(.width(4), .mode("unsigned")) comparator_6 (
    .a(input_2), .b(4'b1011), .gt(comparator_6_gt));  // open: eq, lt
  Multiplexer #(.width(16), .enable("false")) multiplexer_4 (
    .in0({16{1'b0}}), .in1(16'h1), .out(multiplexer_4_out), .sel(comparator_4_gt));
  Multiplexer #(.width(16), .enable("false")) multiplexer_5 (
    .in0(multiplexer_6_out), .in1(16'h1), .out(multiplexer_5_out), .sel(comparator_5_lt));
  // Probe on nothing
  Multiplexer #(.width(16), .enable("false")) multiplexer_6 (
    .in0({16{1'b0}}), .in1({16{1'b1}}), .out(multiplexer_6_out), .sel(comparator_6_gt));
endmodule
