// Logisim project project_demo.circ as structural Verilog: 11 circuits, main circuit main
module main (
  input  [3:0] bus_0,
  input  [3:0] bus_0_2
);

  wire cdm_16_1_p1, cdm_16_1_p2, cdm_16_1_p4, cdm_16_1_p5, cdm_16_1_p6, cdm_16_1_p7, cdm_16_1_p8,
       cdm_16_1_p9, chip_1_out_17, chip_2_out_17, chip_3_out_17, chip_4_out_17, chip_6_out_17, chip_7_out_17,
       chip_8_out_17, chip_9_out_17, chip_10_out_17, chip_11_out_17, chip_12_out_17, chip_13_out_17,
       chip_14_out_17, chip_15_out_17, chip_16_out_17, chip_17_out_17, chip_18_out_17, chip_19_out_17,
       chip_20_out_17, chip_21_out_17, chip_22_out_17, chip_23_out_17, chip_24_out_17, chip_25_out_17,
       chip_26_out_17, chip_27_out_17, chip_28_out_17, chip_29_out_17, chip_30_out_17, chip_31_out_17,
       chip_32_out_17, clock, clock_2_out, comparator_6_eq, mem, not_1_out, rd, word;
  wire [3:0] scoreboard_1_out_2, scoreboard_1_out_3, scoreboard_1_out_4, scoreboard_1_out_5,
       scoreboard_1_out_6, stick_x, stick_y, subtractor_7_out;
  wire [4:0] chip_1_out_9, chip_2_out_9, chip_3_out_9, chip_4_out_9, chip_5_out_9, chip_6_out_9,
       chip_7_out_9, chip_8_out_9, chip_9_out_9, chip_10_out_9, chip_11_out_9, chip_12_out_9, chip_13_out_9,
       chip_14_out_9, chip_15_out_9, chip_16_out_9, chip_17_out_9, chip_18_out_9, chip_19_out_9,
       chip_20_out_9, chip_21_out_9, chip_22_out_9, chip_23_out_9, chip_24_out_9, chip_25_out_9,
       chip_26_out_9, chip_27_out_9, chip_28_out_9, chip_29_out_9, chip_30_out_9, chip_32_out_9,
       subtractor_3_out;
  wire [5:5] comparator_1_lt, comparator_2_lt, comparator_3_lt, comparator_4_lt, comparator_5_lt;
  wire [10:0] chip_1_sprite1_2, chip_1_sprite2_2, chip_1_sprite3_2, chip_1_sprite4_2, chip_1_sprite5_2,
       chip_2_sprite1_2, chip_2_sprite2_2, chip_2_sprite3_2, chip_2_sprite4_2, chip_2_sprite5_2,
       chip_3_sprite1_2, chip_3_sprite2_2, chip_3_sprite3_2, chip_3_sprite4_2, chip_3_sprite5_2,
       chip_4_sprite1_2, chip_4_sprite2_2, chip_4_sprite3_2, chip_4_sprite4_2, chip_4_sprite5_2,
       chip_5_sprite1_2, chip_5_sprite2_2, chip_5_sprite3_2, chip_5_sprite4_2, chip_5_sprite5_2,
       chip_6_sprite1_2, chip_6_sprite2_2, chip_6_sprite3_2, chip_6_sprite4_2, chip_6_sprite5_2,
       chip_7_sprite1_2, chip_7_sprite2_2, chip_7_sprite3_2, chip_7_sprite4_2, chip_7_sprite5_2,
       chip_8_sprite1_2, chip_8_sprite2_2, chip_8_sprite3_2, chip_8_sprite4_2, chip_8_sprite5_2,
       chip_9_sprite1_2, chip_9_sprite2_2, chip_9_sprite3_2, chip_9_sprite4_2, chip_9_sprite5_2,
       chip_10_sprite1_2, chip_10_sprite2_2, chip_10_sprite3_2, chip_10_sprite4_2, chip_10_sprite5_2,
       chip_11_sprite1_2, chip_11_sprite2_2, chip_11_sprite3_2, chip_11_sprite4_2, chip_11_sprite5_2,
       chip_12_sprite1_2, chip_12_sprite2_2, chip_12_sprite3_2, chip_12_sprite4_2, chip_12_sprite5_2,
       chip_13_sprite1_2, chip_13_sprite2_2, chip_13_sprite3_2, chip_13_sprite4_2, chip_13_sprite5_2,
       chip_14_sprite1_2, chip_14_sprite2_2, chip_14_sprite3_2, chip_14_sprite4_2, chip_14_sprite5_2,
       chip_15_sprite1_2, chip_15_sprite2_2, chip_15_sprite3_2, chip_15_sprite4_2, chip_15_sprite5_2,
       chip_16_sprite1_2, chip_16_sprite2_2, chip_16_sprite3_2, chip_16_sprite4_2, chip_16_sprite5_2,
       chip_17_sprite1_2, chip_17_sprite2_2, chip_17_sprite3_2, chip_17_sprite4_2, chip_17_sprite5_2,
       chip_18_sprite1_2, chip_18_sprite2_2, chip_18_sprite3_2, chip_18_sprite4_2, chip_18_sprite5_2,
       chip_19_sprite1_2, chip_19_sprite2_2, chip_19_sprite3_2, chip_19_sprite4_2, chip_19_sprite5_2,
       chip_20_sprite1_2, chip_20_sprite2_2, chip_20_sprite3_2, chip_20_sprite4_2, chip_20_sprite5_2,
       chip_21_sprite1_2, chip_21_sprite2_2, chip_21_sprite3_2, chip_21_sprite4_2, chip_21_sprite5_2,
       chip_22_sprite1_2, chip_22_sprite2_2, chip_22_sprite3_2, chip_22_sprite4_2, chip_22_sprite5_2,
       chip_23_sprite1_2, chip_23_sprite2_2, chip_23_sprite3_2, chip_23_sprite4_2, chip_23_sprite5_2,
       chip_24_sprite1_2, chip_24_sprite2_2, chip_24_sprite3_2, chip_24_sprite4_2, chip_24_sprite5_2,
       chip_25_sprite1_2, chip_25_sprite2_2, chip_25_sprite3_2, chip_25_sprite4_2, chip_25_sprite5_2,
       chip_26_sprite1_2, chip_26_sprite2_2, chip_26_sprite3_2, chip_26_sprite4_2, chip_26_sprite5_2,
       chip_27_sprite1_2, chip_27_sprite2_2, chip_27_sprite3_2, chip_27_sprite4_2, chip_27_sprite5_2,
       chip_28_sprite1_2, chip_28_sprite2_2, chip_28_sprite3_2, chip_28_sprite4_2, chip_28_sprite5_2,
       chip_29_sprite1_2, chip_29_sprite2_2, chip_29_sprite3_2, chip_29_sprite4_2, chip_29_sprite5_2,
       chip_30_sprite1_2, chip_30_sprite2_2, chip_30_sprite3_2, chip_30_sprite4_2, chip_30_sprite5_2,
       chip_32_sprite1_2, chip_32_sprite2_2, chip_32_sprite3_2, chip_32_sprite4_2, chip_32_sprite5_2;
  wire [15:0] _1t1_x, _1t1_y, _1t2_x, _1t2_y, _2t1_x, _2t1_y, _2t2_x, _2t2_y, _2t3_x, _2t3_y, _12, addr,
       cdm_16_1_p15, chip_1_out_16, chip_2_out_16, chip_3_out_16, chip_4_out_16, chip_6_out_16,
       chip_7_out_16, chip_8_out_16, chip_9_out_16, chip_10_out_16, chip_11_out_16, chip_12_out_16,
       chip_13_out_16, chip_14_out_16, chip_15_out_16, chip_16_out_16, chip_17_out_16, chip_18_out_16,
       chip_19_out_16, chip_20_out_16, chip_21_out_16, chip_22_out_16, chip_23_out_16, chip_24_out_16,
       chip_25_out_16, chip_26_out_16, chip_27_out_16, chip_28_out_16, chip_29_out_16, chip_30_out_16,
       chip_31_out_16, chip_32_out_16, column, controlled_buffer_1_out, counter, data,
       distribute_regs_1_bus_0_14, mario_x, mario_y, multiplexer_1_out, out, shifter_1_out, signal,
       subtractor_1_out, subtractor_2_out, subtractor_4_out, subtractor_6_out;
  wire [15:5] subtractor_3_out_2;
  wire [31:0] chip_1_out_11, chip_2_out_11, chip_3_out_11, chip_4_out_11, chip_5_out_11, chip_6_out_11,
       chip_7_out_11, chip_8_out_11, chip_9_out_11, chip_10_out_11, chip_11_out_11, chip_12_out_11,
       chip_13_out_11, chip_14_out_11, chip_15_out_11, chip_16_out_11, chip_17_out_11, chip_18_out_11,
       chip_19_out_11, chip_20_out_11, chip_21_out_11, chip_22_out_11, chip_23_out_11, chip_24_out_11,
       chip_25_out_11, chip_26_out_11, chip_27_out_11, chip_28_out_11, chip_29_out_11, chip_30_out_11,
       chip_31_out_11, chip_32_out_11;

  Comparator #(.width(16)) comparator_1 (.a(mario_x), .b(16'h1d), .lt(comparator_1_lt[5]));  // open: gt, eq
  Comparator #(.width(16)) comparator_2 (.a(_2t2_x), .b(16'h1d), .lt(comparator_2_lt[5]));  // open: gt, eq
  Comparator #(.width(16)) comparator_3 (.a(_1t1_x), .b(16'h1d), .lt(comparator_3_lt[5]));  // open: gt, eq
  // Probe on cdm_16_1_p5
  // Probe on cdm_16_1_p6
  // Probe on cdm_16_1_p4
  // Probe on cdm_16_1_p2
  // CdM_16 cdm_16_1: pin names not known; wires that end beside it: cdm_16_1_p1, cdm_16_1_p2, clock, cdm_16_1_p4, cdm_16_1_p5, cdm_16_1_p6, cdm_16_1_p7, cdm_16_1_p8, cdm_16_1_p9, mem, rd, word, addr, out, cdm_16_1_p15
  // Probe on cdm_16_1_p1
  Clock clock_1 (.out(clock));
  Comparator #(.width(16)) comparator_4 (.a(_2t1_x), .b(16'h1d), .lt(comparator_4_lt[5]));  // open: gt, eq
  // Probe on cdm_16_1_p8
  // Probe on cdm_16_1_p7
  Hex_Digit_Display hex_digit_display_1 (.value(scoreboard_1_out_2));  // open: dp
  // Probe on counter[13:0]
  Subtractor #(.width(16)) subtractor_1 (.a(16'h1d), .b(mario_y), .out(subtractor_1_out));  // open: bin, bout
  Subtractor #(.width(16)) subtractor_2 (.a(16'h1d), .b(_2t1_y), .out(subtractor_2_out));  // open: bin, bout
  Subtractor #(.width(16)) subtractor_3 (
    .a(16'h1d), .b(_2t2_y), .out({subtractor_3_out_2, subtractor_3_out}));  // open: bin, bout
  // Probe on cdm_16_1_p9
  assign controlled_buffer_1_out = rd ? data : 16'bz;  // Controlled_Buffer controlled_buffer_1
  joystick joystick_1 (
    .bus_0(cdm_16_1_p15), .input_1(stick_x), .input_2(stick_y), .addr(addr), .data(controlled_buffer_1_out),
    .mem(mem), .rd(rd));
  Hex_Digit_Display hex_digit_display_2 (.value(scoreboard_1_out_6));  // open: dp
  Hex_Digit_Display hex_digit_display_3 (.value(scoreboard_1_out_4));  // open: dp
  scoreboard scoreboard_1 (
    .in_1(counter[13:0]), .out_3(scoreboard_1_out_3), .out_4(scoreboard_1_out_4), .out_5(scoreboard_1_out_5),
    .out_6(scoreboard_1_out_6), .out_2(scoreboard_1_out_2));
  Subtractor #(.width(16)) subtractor_4 (.a(16'h1d), .b(_1t1_y), .out(subtractor_4_out));  // open: bin, bout
  Comparator #(.width(16)) comparator_5 (.a(_1t2_x), .b(16'h1d), .lt(comparator_5_lt[5]));  // open: gt, eq
  not not_1 (not_1_out, rd);
  assign data = not_1_out ? out : 16'bz;  // Controlled_Buffer controlled_buffer_2
  Subtractor #(.width(16)) subtractor_5 (.a(distribute_regs_1_bus_0_14), .b(16'h1), .out(column));  // open: bin, bout
  Hex_Digit_Display hex_digit_display_4 (.value(scoreboard_1_out_3));  // open: dp
  Hex_Digit_Display hex_digit_display_5 (.value(scoreboard_1_out_5));  // open: dp
  // Probe on _2t3_y
  // Probe on _2t3_x
  Subtractor #(.width(16)) subtractor_6 (.a(16'h1d), .b(_1t2_y), .out(subtractor_6_out));  // open: bin, bout
  // Debugger debugger_1: pin names not known
  // Probe on addr
  DotMatrix #(.matrixcols(32), .matrixrows(32)) dotmatrix_1 (
    .col0(chip_5_out_11), .col1(chip_2_out_11), .col2(chip_1_out_11), .col3(chip_4_out_11),
    .col4(chip_3_out_11), .col5(chip_6_out_11), .col6(chip_8_out_11), .col7(chip_13_out_11),
    .col8(chip_7_out_11), .col9(chip_9_out_11), .col10(chip_11_out_11), .col11(chip_12_out_11),
    .col12(chip_10_out_11), .col13(chip_14_out_11), .col14(chip_16_out_11), .col15(chip_19_out_11),
    .col16(chip_17_out_11), .col17(chip_18_out_11), .col18(chip_15_out_11), .col19(chip_21_out_11),
    .col20(chip_20_out_11), .col21(chip_27_out_11), .col22(chip_29_out_11), .col23(chip_24_out_11),
    .col24(chip_22_out_11), .col25(chip_25_out_11), .col26(chip_23_out_11), .col27(chip_28_out_11),
    .col28(chip_26_out_11), .col29(chip_32_out_11), .col30(chip_30_out_11), .col31(chip_31_out_11));
  chip chip_1 (
    .in_1(chip_2_out_9), .sprite1(chip_2_sprite1_2), .sprite2(chip_2_sprite2_2), .sprite3(chip_2_sprite3_2),
    .out_9(chip_1_out_9), .out_11(chip_1_out_11), .sprite3_2(chip_1_sprite3_2), .sprite1_2(chip_1_sprite1_2),
    .sprite2_2(chip_1_sprite2_2), .in_8(chip_4_out_17), .out_16(chip_1_out_16), .in_7(chip_4_out_16),
    .out_17(chip_1_out_17), .sprite4_2(chip_1_sprite4_2), .sprite4(chip_2_sprite4_2),
    .sprite5_2(chip_1_sprite5_2), .sprite5(chip_2_sprite5_2));
  chip chip_2 (
    .in_1(chip_5_out_9), .sprite1(chip_5_sprite1_2), .sprite2(chip_5_sprite2_2), .sprite3(chip_5_sprite3_2),
    .out_9(chip_2_out_9), .out_11(chip_2_out_11), .sprite3_2(chip_2_sprite3_2), .sprite1_2(chip_2_sprite1_2),
    .sprite2_2(chip_2_sprite2_2), .in_8(chip_1_out_17), .out_16(chip_2_out_16), .in_7(chip_1_out_16),
    .out_17(chip_2_out_17), .sprite4_2(chip_2_sprite4_2), .sprite4(chip_5_sprite4_2),
    .sprite5_2(chip_2_sprite5_2), .sprite5(chip_5_sprite5_2));
  chip chip_3 (
    .in_1(chip_4_out_9), .sprite1(chip_4_sprite1_2), .sprite2(chip_4_sprite2_2), .sprite3(chip_4_sprite3_2),
    .out_9(chip_3_out_9), .out_11(chip_3_out_11), .sprite3_2(chip_3_sprite3_2), .sprite1_2(chip_3_sprite1_2),
    .sprite2_2(chip_3_sprite2_2), .in_8(chip_6_out_17), .out_16(chip_3_out_16), .in_7(chip_6_out_16),
    .out_17(chip_3_out_17), .sprite4_2(chip_3_sprite4_2), .sprite4(chip_4_sprite4_2),
    .sprite5_2(chip_3_sprite5_2), .sprite5(chip_4_sprite5_2));
  chip chip_4 (
    .in_1(chip_1_out_9), .sprite1(chip_1_sprite1_2), .sprite2(chip_1_sprite2_2), .sprite3(chip_1_sprite3_2),
    .out_9(chip_4_out_9), .out_11(chip_4_out_11), .sprite3_2(chip_4_sprite3_2), .sprite1_2(chip_4_sprite1_2),
    .sprite2_2(chip_4_sprite2_2), .in_8(chip_3_out_17), .out_16(chip_4_out_16), .in_7(chip_3_out_16),
    .out_17(chip_4_out_17), .sprite4_2(chip_4_sprite4_2), .sprite4(chip_1_sprite4_2),
    .sprite5_2(chip_4_sprite5_2), .sprite5(chip_1_sprite5_2));
  chip chip_5 (
    .in_1({5{1'b0}}), .sprite1({subtractor_1_out[4:0], comparator_1_lt[5], mario_x[4:0]}),
    .sprite2({subtractor_2_out[4:0], comparator_4_lt[5], _2t1_x[4:0]}),
    .sprite3({subtractor_3_out, comparator_2_lt[5], _2t2_x[4:0]}), .out_9(chip_5_out_9),
    .out_11(chip_5_out_11), .sprite3_2(chip_5_sprite3_2), .sprite1_2(chip_5_sprite1_2),
    .sprite2_2(chip_5_sprite2_2), .in_8(chip_2_out_17), .in_7(chip_2_out_16), .sprite4_2(chip_5_sprite4_2),
    .sprite4({subtractor_4_out[4:0], comparator_3_lt[5], _1t1_x[4:0]}), .sprite5_2(chip_5_sprite5_2),
    .sprite5({subtractor_6_out[4:0], comparator_5_lt[5], _1t2_x[4:0]}));  // open: out_16, out_17
  chip chip_6 (
    .in_1(chip_3_out_9), .sprite1(chip_3_sprite1_2), .sprite2(chip_3_sprite2_2), .sprite3(chip_3_sprite3_2),
    .out_9(chip_6_out_9), .out_11(chip_6_out_11), .sprite3_2(chip_6_sprite3_2), .sprite1_2(chip_6_sprite1_2),
    .sprite2_2(chip_6_sprite2_2), .in_8(chip_8_out_17), .out_16(chip_6_out_16), .in_7(chip_8_out_16),
    .out_17(chip_6_out_17), .sprite4_2(chip_6_sprite4_2), .sprite4(chip_3_sprite4_2),
    .sprite5_2(chip_6_sprite5_2), .sprite5(chip_3_sprite5_2));
  chip chip_7 (
    .in_1(chip_13_out_9), .sprite1(chip_13_sprite1_2), .sprite2(chip_13_sprite2_2),
    .sprite3(chip_13_sprite3_2), .out_9(chip_7_out_9), .out_11(chip_7_out_11), .sprite3_2(chip_7_sprite3_2),
    .sprite1_2(chip_7_sprite1_2), .sprite2_2(chip_7_sprite2_2), .in_8(chip_9_out_17), .out_16(chip_7_out_16),
    .in_7(chip_9_out_16), .out_17(chip_7_out_17), .sprite4_2(chip_7_sprite4_2), .sprite4(chip_13_sprite4_2),
    .sprite5_2(chip_7_sprite5_2), .sprite5(chip_13_sprite5_2));
  chip chip_8 (
    .in_1(chip_6_out_9), .sprite1(chip_6_sprite1_2), .sprite2(chip_6_sprite2_2), .sprite3(chip_6_sprite3_2),
    .out_9(chip_8_out_9), .out_11(chip_8_out_11), .sprite3_2(chip_8_sprite3_2), .sprite1_2(chip_8_sprite1_2),
    .sprite2_2(chip_8_sprite2_2), .in_8(chip_13_out_17), .out_16(chip_8_out_16), .in_7(chip_13_out_16),
    .out_17(chip_8_out_17), .sprite4_2(chip_8_sprite4_2), .sprite4(chip_6_sprite4_2),
    .sprite5_2(chip_8_sprite5_2), .sprite5(chip_6_sprite5_2));
  chip chip_9 (
    .in_1(chip_7_out_9), .sprite1(chip_7_sprite1_2), .sprite2(chip_7_sprite2_2), .sprite3(chip_7_sprite3_2),
    .out_9(chip_9_out_9), .out_11(chip_9_out_11), .sprite3_2(chip_9_sprite3_2), .sprite1_2(chip_9_sprite1_2),
    .sprite2_2(chip_9_sprite2_2), .in_8(chip_11_out_17), .out_16(chip_9_out_16), .in_7(chip_11_out_16),
    .out_17(chip_9_out_17), .sprite4_2(chip_9_sprite4_2), .sprite4(chip_7_sprite4_2),
    .sprite5_2(chip_9_sprite5_2), .sprite5(chip_7_sprite5_2));
  chip chip_10 (
    .in_1(chip_12_out_9), .sprite1(chip_12_sprite1_2), .sprite2(chip_12_sprite2_2),
    .sprite3(chip_12_sprite3_2), .out_9(chip_10_out_9), .out_11(chip_10_out_11),
    .sprite3_2(chip_10_sprite3_2), .sprite1_2(chip_10_sprite1_2), .sprite2_2(chip_10_sprite2_2),
    .in_8(chip_14_out_17), .out_16(chip_10_out_16), .in_7(chip_14_out_16), .out_17(chip_10_out_17),
    .sprite4_2(chip_10_sprite4_2), .sprite4(chip_12_sprite4_2), .sprite5_2(chip_10_sprite5_2),
    .sprite5(chip_12_sprite5_2));
  chip chip_11 (
    .in_1(chip_9_out_9), .sprite1(chip_9_sprite1_2), .sprite2(chip_9_sprite2_2), .sprite3(chip_9_sprite3_2),
    .out_9(chip_11_out_9), .out_11(chip_11_out_11), .sprite3_2(chip_11_sprite3_2),
    .sprite1_2(chip_11_sprite1_2), .sprite2_2(chip_11_sprite2_2), .in_8(chip_12_out_17),
    .out_16(chip_11_out_16), .in_7(chip_12_out_16), .out_17(chip_11_out_17), .sprite4_2(chip_11_sprite4_2),
    .sprite4(chip_9_sprite4_2), .sprite5_2(chip_11_sprite5_2), .sprite5(chip_9_sprite5_2));
  chip chip_12 (
    .in_1(chip_11_out_9), .sprite1(chip_11_sprite1_2), .sprite2(chip_11_sprite2_2),
    .sprite3(chip_11_sprite3_2), .out_9(chip_12_out_9), .out_11(chip_12_out_11),
    .sprite3_2(chip_12_sprite3_2), .sprite1_2(chip_12_sprite1_2), .sprite2_2(chip_12_sprite2_2),
    .in_8(chip_10_out_17), .out_16(chip_12_out_16), .in_7(chip_10_out_16), .out_17(chip_12_out_17),
    .sprite4_2(chip_12_sprite4_2), .sprite4(chip_11_sprite4_2), .sprite5_2(chip_12_sprite5_2),
    .sprite5(chip_11_sprite5_2));
  chip chip_13 (
    .in_1(chip_8_out_9), .sprite1(chip_8_sprite1_2), .sprite2(chip_8_sprite2_2), .sprite3(chip_8_sprite3_2),
    .out_9(chip_13_out_9), .out_11(chip_13_out_11), .sprite3_2(chip_13_sprite3_2),
    .sprite1_2(chip_13_sprite1_2), .sprite2_2(chip_13_sprite2_2), .in_8(chip_7_out_17),
    .out_16(chip_13_out_16), .in_7(chip_7_out_16), .out_17(chip_13_out_17), .sprite4_2(chip_13_sprite4_2),
    .sprite4(chip_8_sprite4_2), .sprite5_2(chip_13_sprite5_2), .sprite5(chip_8_sprite5_2));
  // Probe on column
  // Probe on signal
  // Probe on mario_x
  distribute_regs distribute_regs_1 (
    .addr(addr), .out(out), .bus_0(mario_x), .clock(clock), .bus_0_2(mario_y), .bus_0_3(_1t1_x),
    .bus_0_4(_1t1_y), .bus_0_5(_1t2_x), .bus_0_6(_1t2_y), .bus_0_7(_2t1_x), .mem(mem), .bus_0_8(_2t1_y),
    .bus_0_9(_2t2_x), .bus_0_10(_2t2_y), .bus_0_11(_2t3_x), .bus_0_12(_2t3_y), .bus_0_13(signal),
    .bus_0_14(distribute_regs_1_bus_0_14), .bus_0_15(_12), .bus_0_16(counter), .rd(rd));
  chip chip_14 (
    .in_1(chip_10_out_9), .sprite1(chip_10_sprite1_2), .sprite2(chip_10_sprite2_2),
    .sprite3(chip_10_sprite3_2), .out_9(chip_14_out_9), .out_11(chip_14_out_11),
    .sprite3_2(chip_14_sprite3_2), .sprite1_2(chip_14_sprite1_2), .sprite2_2(chip_14_sprite2_2),
    .in_8(chip_16_out_17), .out_16(chip_14_out_16), .in_7(chip_16_out_16), .out_17(chip_14_out_17),
    .sprite4_2(chip_14_sprite4_2), .sprite4(chip_10_sprite4_2), .sprite5_2(chip_14_sprite5_2),
    .sprite5(chip_10_sprite5_2));
  chip chip_15 (
    .in_1(chip_18_out_9), .sprite1(chip_18_sprite1_2), .sprite2(chip_18_sprite2_2),
    .sprite3(chip_18_sprite3_2), .out_9(chip_15_out_9), .out_11(chip_15_out_11),
    .sprite3_2(chip_15_sprite3_2), .sprite1_2(chip_15_sprite1_2), .sprite2_2(chip_15_sprite2_2),
    .in_8(chip_21_out_17), .out_16(chip_15_out_16), .in_7(chip_21_out_16), .out_17(chip_15_out_17),
    .sprite4_2(chip_15_sprite4_2), .sprite4(chip_18_sprite4_2), .sprite5_2(chip_15_sprite5_2),
    .sprite5(chip_18_sprite5_2));
  chip chip_16 (
    .in_1(chip_14_out_9), .sprite1(chip_14_sprite1_2), .sprite2(chip_14_sprite2_2),
    .sprite3(chip_14_sprite3_2), .out_9(chip_16_out_9), .out_11(chip_16_out_11),
    .sprite3_2(chip_16_sprite3_2), .sprite1_2(chip_16_sprite1_2), .sprite2_2(chip_16_sprite2_2),
    .in_8(chip_19_out_17), .out_16(chip_16_out_16), .in_7(chip_19_out_16), .out_17(chip_16_out_17),
    .sprite4_2(chip_16_sprite4_2), .sprite4(chip_14_sprite4_2), .sprite5_2(chip_16_sprite5_2),
    .sprite5(chip_14_sprite5_2));
  chip chip_17 (
    .in_1(chip_19_out_9), .sprite1(chip_19_sprite1_2), .sprite2(chip_19_sprite2_2),
    .sprite3(chip_19_sprite3_2), .out_9(chip_17_out_9), .out_11(chip_17_out_11),
    .sprite3_2(chip_17_sprite3_2), .sprite1_2(chip_17_sprite1_2), .sprite2_2(chip_17_sprite2_2),
    .in_8(chip_18_out_17), .out_16(chip_17_out_16), .in_7(chip_18_out_16), .out_17(chip_17_out_17),
    .sprite4_2(chip_17_sprite4_2), .sprite4(chip_19_sprite4_2), .sprite5_2(chip_17_sprite5_2),
    .sprite5(chip_19_sprite5_2));
  chip chip_18 (
    .in_1(chip_17_out_9), .sprite1(chip_17_sprite1_2), .sprite2(chip_17_sprite2_2),
    .sprite3(chip_17_sprite3_2), .out_9(chip_18_out_9), .out_11(chip_18_out_11),
    .sprite3_2(chip_18_sprite3_2), .sprite1_2(chip_18_sprite1_2), .sprite2_2(chip_18_sprite2_2),
    .in_8(chip_15_out_17), .out_16(chip_18_out_16), .in_7(chip_15_out_16), .out_17(chip_18_out_17),
    .sprite4_2(chip_18_sprite4_2), .sprite4(chip_17_sprite4_2), .sprite5_2(chip_18_sprite5_2),
    .sprite5(chip_17_sprite5_2));
  chip chip_19 (
    .in_1(chip_16_out_9), .sprite1(chip_16_sprite1_2), .sprite2(chip_16_sprite2_2),
    .sprite3(chip_16_sprite3_2), .out_9(chip_19_out_9), .out_11(chip_19_out_11),
    .sprite3_2(chip_19_sprite3_2), .sprite1_2(chip_19_sprite1_2), .sprite2_2(chip_19_sprite2_2),
    .in_8(chip_17_out_17), .out_16(chip_19_out_16), .in_7(chip_17_out_16), .out_17(chip_19_out_17),
    .sprite4_2(chip_19_sprite4_2), .sprite4(chip_16_sprite4_2), .sprite5_2(chip_19_sprite5_2),
    .sprite5(chip_16_sprite5_2));
  chip chip_20 (
    .in_1(chip_21_out_9), .sprite1(chip_21_sprite1_2), .sprite2(chip_21_sprite2_2),
    .sprite3(chip_21_sprite3_2), .out_9(chip_20_out_9), .out_11(chip_20_out_11),
    .sprite3_2(chip_20_sprite3_2), .sprite1_2(chip_20_sprite1_2), .sprite2_2(chip_20_sprite2_2),
    .in_8(chip_27_out_17), .out_16(chip_20_out_16), .in_7(chip_27_out_16), .out_17(chip_20_out_17),
    .sprite4_2(chip_20_sprite4_2), .sprite4(chip_21_sprite4_2), .sprite5_2(chip_20_sprite5_2),
    .sprite5(chip_21_sprite5_2));
  chip chip_21 (
    .in_1(chip_15_out_9), .sprite1(chip_15_sprite1_2), .sprite2(chip_15_sprite2_2),
    .sprite3(chip_15_sprite3_2), .out_9(chip_21_out_9), .out_11(chip_21_out_11),
    .sprite3_2(chip_21_sprite3_2), .sprite1_2(chip_21_sprite1_2), .sprite2_2(chip_21_sprite2_2),
    .in_8(chip_20_out_17), .out_16(chip_21_out_16), .in_7(chip_20_out_16), .out_17(chip_21_out_17),
    .sprite4_2(chip_21_sprite4_2), .sprite4(chip_15_sprite4_2), .sprite5_2(chip_21_sprite5_2),
    .sprite5(chip_15_sprite5_2));
  // Probe on mario_x
  // Probe on mario_y
  // Probe on _1t1_x
  // Probe on _1t1_y
  // Probe on _1t2_x
  // Probe on _1t2_y
  // Probe on _2t1_x
  // Probe on _2t1_y
  // Probe on _2t2_x
  // Probe on _2t2_y
  // Probe on counter
  chip chip_22 (
    .in_1(chip_24_out_9), .sprite1(chip_24_sprite1_2), .sprite2(chip_24_sprite2_2),
    .sprite3(chip_24_sprite3_2), .out_9(chip_22_out_9), .out_11(chip_22_out_11),
    .sprite3_2(chip_22_sprite3_2), .sprite1_2(chip_22_sprite1_2), .sprite2_2(chip_22_sprite2_2),
    .in_8(chip_25_out_17), .out_16(chip_22_out_16), .in_7(chip_25_out_16), .out_17(chip_22_out_17),
    .sprite4_2(chip_22_sprite4_2), .sprite4(chip_24_sprite4_2), .sprite5_2(chip_22_sprite5_2),
    .sprite5(chip_24_sprite5_2));
  chip chip_23 (
    .in_1(chip_25_out_9), .sprite1(chip_25_sprite1_2), .sprite2(chip_25_sprite2_2),
    .sprite3(chip_25_sprite3_2), .out_9(chip_23_out_9), .out_11(chip_23_out_11),
    .sprite3_2(chip_23_sprite3_2), .sprite1_2(chip_23_sprite1_2), .sprite2_2(chip_23_sprite2_2),
    .in_8(chip_28_out_17), .out_16(chip_23_out_16), .in_7(chip_28_out_16), .out_17(chip_23_out_17),
    .sprite4_2(chip_23_sprite4_2), .sprite4(chip_25_sprite4_2), .sprite5_2(chip_23_sprite5_2),
    .sprite5(chip_25_sprite5_2));
  chip chip_24 (
    .in_1(chip_29_out_9), .sprite1(chip_29_sprite1_2), .sprite2(chip_29_sprite2_2),
    .sprite3(chip_29_sprite3_2), .out_9(chip_24_out_9), .out_11(chip_24_out_11),
    .sprite3_2(chip_24_sprite3_2), .sprite1_2(chip_24_sprite1_2), .sprite2_2(chip_24_sprite2_2),
    .in_8(chip_22_out_17), .out_16(chip_24_out_16), .in_7(chip_22_out_16), .out_17(chip_24_out_17),
    .sprite4_2(chip_24_sprite4_2), .sprite4(chip_29_sprite4_2), .sprite5_2(chip_24_sprite5_2),
    .sprite5(chip_29_sprite5_2));
  chip chip_25 (
    .in_1(chip_22_out_9), .sprite1(chip_22_sprite1_2), .sprite2(chip_22_sprite2_2),
    .sprite3(chip_22_sprite3_2), .out_9(chip_25_out_9), .out_11(chip_25_out_11),
    .sprite3_2(chip_25_sprite3_2), .sprite1_2(chip_25_sprite1_2), .sprite2_2(chip_25_sprite2_2),
    .in_8(chip_23_out_17), .out_16(chip_25_out_16), .in_7(chip_23_out_16), .out_17(chip_25_out_17),
    .sprite4_2(chip_25_sprite4_2), .sprite4(chip_22_sprite4_2), .sprite5_2(chip_25_sprite5_2),
    .sprite5(chip_22_sprite5_2));
  chip chip_26 (
    .in_1(chip_28_out_9), .sprite1(chip_28_sprite1_2), .sprite2(chip_28_sprite2_2),
    .sprite3(chip_28_sprite3_2), .out_9(chip_26_out_9), .out_11(chip_26_out_11),
    .sprite3_2(chip_26_sprite3_2), .sprite1_2(chip_26_sprite1_2), .sprite2_2(chip_26_sprite2_2),
    .in_8(chip_32_out_17), .out_16(chip_26_out_16), .in_7(chip_32_out_16), .out_17(chip_26_out_17),
    .sprite4_2(chip_26_sprite4_2), .sprite4(chip_28_sprite4_2), .sprite5_2(chip_26_sprite5_2),
    .sprite5(chip_28_sprite5_2));
  chip chip_27 (
    .in_1(chip_20_out_9), .sprite1(chip_20_sprite1_2), .sprite2(chip_20_sprite2_2),
    .sprite3(chip_20_sprite3_2), .out_9(chip_27_out_9), .out_11(chip_27_out_11),
    .sprite3_2(chip_27_sprite3_2), .sprite1_2(chip_27_sprite1_2), .sprite2_2(chip_27_sprite2_2),
    .in_8(chip_29_out_17), .out_16(chip_27_out_16), .in_7(chip_29_out_16), .out_17(chip_27_out_17),
    .sprite4_2(chip_27_sprite4_2), .sprite4(chip_20_sprite4_2), .sprite5_2(chip_27_sprite5_2),
    .sprite5(chip_20_sprite5_2));
  chip chip_28 (
    .in_1(chip_23_out_9), .sprite1(chip_23_sprite1_2), .sprite2(chip_23_sprite2_2),
    .sprite3(chip_23_sprite3_2), .out_9(chip_28_out_9), .out_11(chip_28_out_11),
    .sprite3_2(chip_28_sprite3_2), .sprite1_2(chip_28_sprite1_2), .sprite2_2(chip_28_sprite2_2),
    .in_8(chip_26_out_17), .out_16(chip_28_out_16), .in_7(chip_26_out_16), .out_17(chip_28_out_17),
    .sprite4_2(chip_28_sprite4_2), .sprite4(chip_23_sprite4_2), .sprite5_2(chip_28_sprite5_2),
    .sprite5(chip_23_sprite5_2));
  chip chip_29 (
    .in_1(chip_27_out_9), .sprite1(chip_27_sprite1_2), .sprite2(chip_27_sprite2_2),
    .sprite3(chip_27_sprite3_2), .out_9(chip_29_out_9), .out_11(chip_29_out_11),
    .sprite3_2(chip_29_sprite3_2), .sprite1_2(chip_29_sprite1_2), .sprite2_2(chip_29_sprite2_2),
    .in_8(chip_24_out_17), .out_16(chip_29_out_16), .in_7(chip_24_out_16), .out_17(chip_29_out_17),
    .sprite4_2(chip_29_sprite4_2), .sprite4(chip_27_sprite4_2), .sprite5_2(chip_29_sprite5_2),
    .sprite5(chip_27_sprite5_2));
  chip chip_30 (
    .in_1(chip_32_out_9), .sprite1(chip_32_sprite1_2), .sprite2(chip_32_sprite2_2),
    .sprite3(chip_32_sprite3_2), .out_9(chip_30_out_9), .out_11(chip_30_out_11),
    .sprite3_2(chip_30_sprite3_2), .sprite1_2(chip_30_sprite1_2), .sprite2_2(chip_30_sprite2_2),
    .in_8(chip_31_out_17), .out_16(chip_30_out_16), .in_7(chip_31_out_16), .out_17(chip_30_out_17),
    .sprite4_2(chip_30_sprite4_2), .sprite4(chip_32_sprite4_2), .sprite5_2(chip_30_sprite5_2),
    .sprite5(chip_32_sprite5_2));
  chip chip_31 (
    .in_1(chip_30_out_9), .sprite1(chip_30_sprite1_2), .sprite2(chip_30_sprite2_2),
    .sprite3(chip_30_sprite3_2), .out_11(chip_31_out_11), .in_8(signal[1]), .out_16(chip_31_out_16),
    .in_7(multiplexer_1_out), .out_17(chip_31_out_17), .sprite4(chip_30_sprite4_2),
    .sprite5(chip_30_sprite5_2));  // open: out_9, sprite3_2, sprite1_2, sprite2_2, sprite4_2, sprite5_2
  chip chip_32 (
    .in_1(chip_26_out_9), .sprite1(chip_26_sprite1_2), .sprite2(chip_26_sprite2_2),
    .sprite3(chip_26_sprite3_2), .out_9(chip_32_out_9), .out_11(chip_32_out_11),
    .sprite3_2(chip_32_sprite3_2), .sprite1_2(chip_32_sprite1_2), .sprite2_2(chip_32_sprite2_2),
    .in_8(chip_30_out_17), .out_16(chip_32_out_16), .in_7(chip_30_out_16), .out_17(chip_32_out_17),
    .sprite4_2(chip_32_sprite4_2), .sprite4(chip_26_sprite4_2), .sprite5_2(chip_32_sprite5_2),
    .sprite5(chip_26_sprite5_2));
  Clock clock_2 (.out(clock_2_out));
  Joystick joystick_2 (.x(stick_x), .y(stick_y));
  // RAM ram_1: pin names not known; wires that end beside it: stick_y, addr, bus_0, bus_0_2, word, mem, clock_2_out, rd, data
  // Probe on stick_x
  // Probe on stick_y
  Subtractor #(.width(4)) subtractor_7 (.a(column[3:0]), .b(4'b0001), .out(subtractor_7_out));  // open: bin, bout
  // Probe on subtractor_7_out
  Multiplexer #(.width(16), .enable("false")) multiplexer_1 (
    .in0(shifter_1_out), .in1({16{1'b0}}), .out(multiplexer_1_out), .sel(comparator_6_eq));
  Shifter #(.width(16)) shifter_1 (.in(16'h1), .\dist (subtractor_7_out), .out(shifter_1_out));
  Comparator #(.width(4)) comparator_6 (.a(column[3:0]), .b(4'b0000), .eq(comparator_6_eq));  // open: gt, lt
endmodule

module scoreboard (
  input  [13:0] in_1,
  output [3:0] out_2,
  output [3:0] out_3,
  output [3:0] out_4,
  output [3:0] out_5,
  output [3:0] out_6
);

  wire [4:1] divider_4_out;
  wire [4:4] divider_4_rem;
  wire [7:0] divider_3_out;
  wire [7:4] divider_3_rem;
  wire [10:0] divider_2_out;
  wire [10:4] divider_2_rem;
  wire [13:0] divider_1_out;
  wire [13:4] divider_1_rem;

  // Probe on 14'ha
  // Probe on in_1
  Divider #(.width(14)) divider_1 (
    .a(in_1), .b(14'ha), .out(divider_1_out), .rem({divider_1_rem, out_5}));  // open: upper
  // Probe on out_5
  // Probe on divider_1_out[10:0]
  Divider #(.width(11)) divider_2 (
    .a(divider_1_out[10:0]), .b(11'ha), .out(divider_2_out), .rem({divider_2_rem, out_3}));  // open: upper
  // Probe on out_3
  // Probe on divider_2_out[7:0]
  // Probe on divider_3_out[4:0]
  Divider divider_3 (
    .a(divider_2_out[7:0]), .b(8'ha), .out(divider_3_out), .rem({divider_3_rem, out_4}));  // open: upper
  // Probe on out_4
  // Probe on out_2[0]
  Divider #(.width(5)) divider_4 (
    .a(divider_3_out[4:0]), .b(5'b01010), .out({divider_4_out, out_2[0]}), .rem({divider_4_rem[4], out_6}));  // open: upper

  assign out_2[3:1] = 3'b000;
endmodule

module chip (
  input  [4:0] in_1,
  input  [10:0] sprite1,
  input  [10:0] sprite2,
  input  [10:0] sprite3,
  input  [10:0] sprite4,
  input  [10:0] sprite5,
  input  [15:0] in_7,
  input  in_8,
  output [4:0] out_9,
  output [10:0] sprite1_2,
  output [31:0] out_11,
  output [10:0] sprite2_2,
  output [10:0] sprite3_2,
  output [10:0] sprite4_2,
  output [10:0] sprite5_2,
  output [15:0] out_16,
  output out_17
);

  wire and_1_out, and_2_out, and_3_out, and_4_out, and_5_out, comparator_1_lt, comparator_2_eq,
       comparator_2_gt, comparator_3_lt, comparator_4_eq, comparator_4_gt, comparator_5_lt, comparator_6_eq,
       comparator_6_gt, comparator_7_lt, comparator_8_eq, comparator_8_gt, comparator_9_lt, comparator_10_eq,
       comparator_10_gt, or_1_out, or_2_out, or_3_out, or_4_out, or_5_out;
  wire [4:0] subtractor_1_out, subtractor_2_out, subtractor_3_out, subtractor_4_out, subtractor_5_out;
  wire [31:0] and_6_out, and_7_out, and_8_out, and_9_out, inventor_1_out_2, inventor_2_out_2,
       inventor_3_out_2, inventor_4_out_2, not_1_out, not_2_out, not_3_out, not_4_out, shifter_1_out,
       shifter_2_out, shifter_3_out, shifter_4_out, shifter_5_out, super_mux2_1_out_3, super_mux2_2_out_3,
       super_mux3_1_out_3, super_mux3_2_out_3, super_mux_1_out_3;

  Adder #(.width(5)) adder_1 (.a(in_1), .b(5'b00001), .out(out_9));  // open: cin, cout
  // Probe on sprite1[4:0]
  // Probe on sprite1[10:6]
  // Probe on sprite2[4:0]
  // Probe on sprite2[10:6]
  // Probe on sprite3[4:0]
  // Probe on sprite3[10:6]
  // Probe on sprite4[4:0]
  // Probe on sprite4[10:6]
  // Probe on sprite5[4:0]
  // Probe on sprite5[10:6]
  Subtractor #(.width(5)) subtractor_1 (.a(out_9), .b(sprite3[4:0]), .out(subtractor_1_out));  // open: bin, bout
  Subtractor #(.width(5)) subtractor_2 (.a(out_9), .b(sprite5[4:0]), .out(subtractor_2_out));  // open: bin, bout
  Subtractor #(.width(5)) subtractor_3 (.a(out_9), .b(sprite1[4:0]), .out(subtractor_3_out));  // open: bin, bout
  Subtractor #(.width(5)) subtractor_4 (.a(out_9), .b(sprite2[4:0]), .out(subtractor_4_out));  // open: bin, bout
  Subtractor #(.width(5)) subtractor_5 (.a(out_9), .b(sprite4[4:0]), .out(subtractor_5_out));  // open: bin, bout
  Comparator #(.width(5)) comparator_1 (.a(subtractor_3_out), .b(5'b00011), .lt(comparator_1_lt));  // open: gt, eq
  Comparator #(.width(5)) comparator_2 (
    .a(subtractor_3_out), .b({5{1'b0}}), .gt(comparator_2_gt), .eq(comparator_2_eq));  // open: lt
  or or_1 (or_1_out, comparator_2_gt, comparator_2_eq);
  Comparator #(.width(5)) comparator_3 (.a(subtractor_4_out), .b(5'b00011), .lt(comparator_3_lt));  // open: gt, eq
  Comparator #(.width(5)) comparator_4 (
    .a(subtractor_4_out), .b({5{1'b0}}), .gt(comparator_4_gt), .eq(comparator_4_eq));  // open: lt
  or or_2 (or_2_out, comparator_4_gt, comparator_4_eq);
  Comparator #(.width(5)) comparator_5 (.a(subtractor_1_out), .b(5'b00011), .lt(comparator_5_lt));  // open: gt, eq
  Comparator #(.width(5)) comparator_6 (
    .a(subtractor_1_out), .b({5{1'b0}}), .gt(comparator_6_gt), .eq(comparator_6_eq));  // open: lt
  or or_3 (or_3_out, comparator_6_gt, comparator_6_eq);
  Comparator #(.width(5)) comparator_7 (.a(subtractor_5_out), .b(5'b00011), .lt(comparator_7_lt));  // open: gt, eq
  or or_4 (or_4_out, comparator_8_gt, comparator_8_eq);
  Comparator #(.width(5)) comparator_8 (
    .a(subtractor_5_out), .b({5{1'b0}}), .gt(comparator_8_gt), .eq(comparator_8_eq));  // open: lt
  Comparator #(.width(5)) comparator_9 (.a(subtractor_2_out), .b(5'b00011), .lt(comparator_9_lt));  // open: gt, eq
  or or_5 (or_5_out, comparator_10_gt, comparator_10_eq);
  Comparator #(.width(5)) comparator_10 (
    .a(subtractor_2_out), .b({5{1'b0}}), .gt(comparator_10_gt), .eq(comparator_10_eq));  // open: lt
  and and_1 (and_1_out, comparator_1_lt, sprite1[5], or_1_out);
  and and_2 (and_2_out, comparator_5_lt, sprite3[5], or_3_out);
  and and_3 (and_3_out, comparator_7_lt, sprite4[5], or_4_out);
  and and_4 (and_4_out, comparator_9_lt, sprite5[5], or_5_out);
  super_mux super_mux_1 (.in_1(and_1_out), .in_2(subtractor_3_out[1:0]), .out_3(super_mux_1_out_3));
  and and_5 (and_5_out, comparator_3_lt, sprite2[5], or_2_out);
  super_mux2 super_mux2_1 (.in_1(and_2_out), .in_2(subtractor_1_out[1:0]), .out_3(super_mux2_1_out_3));
  super_mux3 super_mux3_1 (.in_1(and_3_out), .in_2(subtractor_5_out[1:0]), .out_3(super_mux3_1_out_3));
  super_mux3 super_mux3_2 (.in_1(and_4_out), .in_2(subtractor_2_out[1:0]), .out_3(super_mux3_2_out_3));
  super_mux2 super_mux2_2 (.in_1(and_5_out), .in_2(subtractor_4_out[1:0]), .out_3(super_mux2_2_out_3));
  Register #(.width(16)) register_1 (.D(in_7), .Q(out_16), .clk(in_8));  // open: en, clr
  Shifter #(.width(32), .shift("lr")) shifter_1 (.in(super_mux_1_out_3), .\dist (sprite1[10:6]), .out(shifter_1_out));
  Shifter #(.width(32), .shift("lr")) shifter_2 (.in(super_mux2_2_out_3), .\dist (sprite2[10:6]), .out(shifter_2_out));
  Shifter #(.width(32), .shift("lr")) shifter_3 (.in(super_mux2_1_out_3), .\dist (sprite3[10:6]), .out(shifter_3_out));
  // Probe on shifter_3_out
  Shifter #(.width(32), .shift("lr")) shifter_4 (.in(super_mux3_1_out_3), .\dist (sprite4[10:6]), .out(shifter_4_out));
  // Probe on shifter_5_out
  Shifter #(.width(32), .shift("lr")) shifter_5 (.in(super_mux3_2_out_3), .\dist (sprite5[10:6]), .out(shifter_5_out));
  // Probe on shifter_1_out
  // Probe on shifter_2_out
  // Probe on shifter_4_out
  // Probe on and_9_out
  assign not_1_out = ~shifter_2_out;  // NOT_Gate not_1, 32 bits wide
  assign not_2_out = ~shifter_3_out;  // NOT_Gate not_2, 32 bits wide
  inventor inventor_1 (.in_1(not_2_out), .out_2(inventor_1_out_2));
  inventor inventor_2 (.in_1(not_3_out), .out_2(inventor_2_out_2));
  assign not_3_out = ~shifter_4_out;  // NOT_Gate not_3, 32 bits wide
  assign not_4_out = ~shifter_5_out;  // NOT_Gate not_4, 32 bits wide
  inventor inventor_3 (.in_1(not_4_out), .out_2(inventor_3_out_2));
  inventor inventor_4 (.in_1(not_1_out), .out_2(inventor_4_out_2));
  // Probe on and_6_out
  assign and_6_out = shifter_3_out & inventor_1_out_2;  // AND_Gate and_6, 32 bits wide
  assign and_7_out = shifter_4_out & inventor_2_out_2;  // AND_Gate and_7, 32 bits wide
  // Probe on and_8_out
  assign and_8_out = shifter_5_out & inventor_3_out_2;  // AND_Gate and_8, 32 bits wide
  assign out_11 = shifter_1_out | and_9_out | and_6_out | and_7_out | and_8_out | {{14{1'b0}}, out_16, 2'b11};  // OR_Gate or_6, 32 bits wide
  assign and_9_out = shifter_2_out & inventor_4_out_2;  // AND_Gate and_9, 32 bits wide
  // Probe on and_7_out

  assign out_17 = in_8;
  assign sprite1_2 = sprite1;
  assign sprite2_2 = sprite2;
  assign sprite3_2 = sprite3;
  assign sprite4_2 = sprite4;
  assign sprite5_2 = sprite5;
endmodule

module sprite1 (
  input  [1:0] in_1,
  output [31:0] out_2
);

  Multiplexer #(.select(2), .width(3), .enable("false")) multiplexer_1 (
    .in0(3'b001), .in1(3'b110), .in2(3'b101), .out(out_2[31:29]), .sel(in_1));  // open: in3

  assign out_2[28:0] = {29{1'b0}};
endmodule

module sprite2 (
  input  [1:0] in_1,
  output [31:0] out_2
);

  Multiplexer #(.select(2), .width(3), .enable("false")) multiplexer_1 (
    .in0(3'b111), .in1(3'b010), .in2(3'b011), .out(out_2[31:29]), .sel(in_1));  // open: in3

  assign out_2[28:0] = {29{1'b0}};
endmodule

module sprite3 (
  input  [1:0] in_1,
  output [31:0] out_2
);

  Multiplexer #(.select(2), .width(3), .enable("false")) multiplexer_1 (
    .in0(3'b100), .in1(3'b111), .in2(3'b110), .out(out_2[31:29]), .sel(in_1));  // open: in3

  assign out_2[28:0] = {29{1'b0}};
endmodule

module super_mux (
  input  in_1,
  input  [1:0] in_2,
  output [31:0] out_3
);

  wire [31:0] sprite1_1_out_2;

  sprite1 sprite1_1 (.out_2(sprite1_1_out_2), .in_1(in_2));
  Multiplexer #(.width(32), .enable("false")) multiplexer_1 (
    .in0({32{1'b0}}), .in1(sprite1_1_out_2), .out(out_3), .sel(in_1));
endmodule

module super_mux2 (
  input  in_1,
  input  [1:0] in_2,
  output [31:0] out_3
);

  wire [31:0] sprite2_1_out_2;

  sprite2 sprite2_1 (.out_2(sprite2_1_out_2), .in_1(in_2));
  Multiplexer #(.width(32), .enable("false")) multiplexer_1 (
    .in0({32{1'b0}}), .in1(sprite2_1_out_2), .out(out_3), .sel(in_1));
endmodule

module super_mux3 (
  input  in_1,
  input  [1:0] in_2,
  output [31:0] out_3
);

  wire [31:0] sprite3_1_out_2;

  sprite3 sprite3_1 (.out_2(sprite3_1_out_2), .in_1(in_2));
  Multiplexer #(.width(32), .enable("false")) multiplexer_1 (
    .in0({32{1'b0}}), .in1(sprite3_1_out_2), .out(out_3), .sel(in_1));
endmodule

module inventor (
  input  [31:0] in_1,
  output [31:0] out_2
);

  inv inv_1 (.in_1(in_1[0]), .out_2(out_2[0]));
  inv inv_2 (.in_1(in_1[1]), .out_2(out_2[1]));
  inv inv_3 (.in_1(in_1[2]), .out_2(out_2[2]));
  inv inv_4 (.in_1(in_1[3]), .out_2(out_2[3]));
  inv inv_5 (.in_1(in_1[4]), .out_2(out_2[4]));
  inv inv_6 (.in_1(in_1[5]), .out_2(out_2[5]));
  inv inv_7 (.in_1(in_1[6]), .out_2(out_2[6]));
  inv inv_8 (.in_1(in_1[7]), .out_2(out_2[7]));
  inv inv_9 (.in_1(in_1[8]), .out_2(out_2[8]));
  inv inv_10 (.in_1(in_1[9]), .out_2(out_2[9]));
  inv inv_11 (.in_1(in_1[10]), .out_2(out_2[10]));
  inv inv_12 (.in_1(in_1[11]), .out_2(out_2[11]));
  inv inv_13 (.in_1(in_1[12]), .out_2(out_2[12]));
  inv inv_14 (.in_1(in_1[13]), .out_2(out_2[13]));
  inv inv_15 (.in_1(in_1[14]), .out_2(out_2[14]));
  inv inv_16 (.in_1(in_1[15]), .out_2(out_2[15]));
  inv inv_17 (.in_1(in_1[16]), .out_2(out_2[16]));
  inv inv_18 (.in_1(in_1[17]), .out_2(out_2[17]));
  inv inv_19 (.in_1(in_1[18]), .out_2(out_2[18]));
  inv inv_20 (.in_1(in_1[19]), .out_2(out_2[19]));
  inv inv_21 (.in_1(in_1[20]), .out_2(out_2[20]));
  inv inv_22 (.in_1(in_1[21]), .out_2(out_2[21]));
  inv inv_23 (.in_1(in_1[22]), .out_2(out_2[22]));
  inv inv_24 (.in_1(in_1[23]), .out_2(out_2[23]));
  inv inv_25 (.in_1(in_1[24]), .out_2(out_2[24]));
  inv inv_26 (.in_1(in_1[25]), .out_2(out_2[25]));
  inv inv_27 (.in_1(in_1[26]), .out_2(out_2[26]));
  inv inv_28 (.in_1(in_1[27]), .out_2(out_2[27]));
  inv inv_29 (.in_1(in_1[28]), .out_2(out_2[28]));
  inv inv_30 (.in_1(in_1[29]), .out_2(out_2[29]));
  inv inv_31 (.in_1(in_1[30]), .out_2(out_2[30]));
  inv inv_32 (.in_1(in_1[31]), .out_2(out_2[31]));
endmodule

module inv (
  input  in_1,
  output out_2
);

  assign out_2 = in_1 ? ~in_1 : 1'bz;  // Controlled_Inverter controlled_inverter_1
endmodule
